# Fritzing sketch LDR (saved by Fritzing 0.9.3b)
breadboards: 1

parts:
  R2 = Photocell (LDR) [package=THT]
  R1 = Resistor [tolerance=±5% resistance=10k package=THT]
  Part1 = Arduino Uno (Rev3)

nets:
  N1: R2.pin_0, R1.Pin_1, Part1.A5/SCL
  N2: R2.pin_1, Part1.5V
  N3: R1.Pin_0, Part1.GND
