# Fritzing sketch Capacitor (saved by Fritzing 0.9.3b)
breadboards: 1

parts:
  C1 = Electrolytic Capacitor [capacitance=1µF package="100 mil [THT, electrolytic]"]
  R1 = Resistor [tolerance=±2% resistance=10k package="1206 [SMD]"]
  Part1 = Arduino Uno (Rev3)

nets:
  N1: C1.-, Part1.GND
  N2: C1.+, R1.Pin_0, Part1.A5/SCL, Part1.D7
  N3: R1.Pin_1, Part1.D9_PWM
